// Digital circuit GPR_BANK_PROJECT.dig as structural Verilog
module GPR_BANK_PROJECT (
  input  CLK,
  input  LD,
  input  [7:0] DIN_0,
  input  [7:0] DIN_1,
  input  SRC,
  input  [1:0] WSEL,
  input  [1:0] RSEL,
  input  CLR,
  input  ST,
  output [7:0] R_0,
  output [7:0] R_1,
  output [7:0] R_2,
  output [7:0] R_3,
  output [7:0] R_OUT,
  output [7:0] D_OUT
);

  wire and_1_out, and_2_out, and_3_out, and_4_out, decoder_1_out_0, decoder_1_out_1, decoder_1_out_2,
       decoder_1_out_3;
  wire [7:0] multiplexer_1_out;

  Decoder #(.Selector_Bits(2)) decoder_1 (
    .sel(WSEL), .out_0(decoder_1_out_0), .out_1(decoder_1_out_1), .out_2(decoder_1_out_2),
    .out_3(decoder_1_out_3));
  Multiplexer #(.Bits(8)) multiplexer_1 (.sel(SRC), .in_0(DIN_0), .in_1(DIN_1), .out(multiplexer_1_out));
  and and_1 (and_1_out, decoder_1_out_0, LD);
  and and_2 (and_2_out, decoder_1_out_1, LD);
  and and_3 (and_3_out, decoder_1_out_2, LD);
  and and_4 (and_4_out, decoder_1_out_3, LD);
  REG8_CORE U_R_0 (.D(multiplexer_1_out), .LD(and_1_out), .CLR(CLR), .CLK(CLK), .Q(R_0));
  REG8_CORE U_R_1 (.D(multiplexer_1_out), .LD(and_2_out), .CLR(CLR), .CLK(CLK), .Q(R_1));
  REG8_CORE U_R_2 (.D(multiplexer_1_out), .LD(and_3_out), .CLR(CLR), .CLK(CLK), .Q(R_2));
  REG8_CORE U_R_3 (.D(multiplexer_1_out), .LD(and_4_out), .CLR(CLR), .CLK(CLK), .Q(R_3));
  Multiplexer #(.Selector_Bits(2), .Bits(8)) multiplexer_2 (
    .sel(RSEL), .in_0(R_0), .in_1(R_1), .in_2(R_2), .in_3(R_3), .out(R_OUT));
  assign D_OUT = ST ? R_OUT : 8'bz;  // Driver driver_1
endmodule
