// Digital circuit IR8.dig as structural Verilog
module IR8 (
  input  [7:0] D_IN_0,
  input  [7:0] D_IN_1,
  input  SRC,
  input  CLK,
  input  LD,
  output [7:0] IR
);

  wire [7:0] multiplexer_1_out;

  Multiplexer #(.Bits(8)) multiplexer_1 (.sel(SRC), .in_0(D_IN_0), .in_1(D_IN_1), .out(multiplexer_1_out));
  REG8_CORE reg8_core_1 (.D(multiplexer_1_out), .LD(LD), .CLR(1'b0), .CLK(CLK), .Q(IR));
endmodule
