// Digital circuit PC8.dig as structural Verilog
module PC8 (
  input  INC,
  input  LD,
  input  [7:0] Val,
  input  RST,
  input  CLK,
  output [7:0] PC_7_0
);

  wire or_1_out;
  wire [7:0] add_1_s, multiplexer_1_out;

  or or_1 (or_1_out, INC, LD);
  REG8_CORE reg8_core_1 (.D(multiplexer_1_out), .LD(or_1_out), .CLR(RST), .CLK(CLK), .Q(PC_7_0));
  Add #(.Bits(8)) add_1 (.a(PC_7_0), .b(8'h1), .c_i(1'b0), .s(add_1_s));  // open: c_o
  Multiplexer #(.Bits(8)) multiplexer_1 (.sel(LD), .in_0(add_1_s), .in_1(Val), .out(multiplexer_1_out));
endmodule
