// Digital circuit REG8_CORE.dig as structural Verilog
module REG8_CORE (
  input  [7:0] D,
  input  LD,
  input  CLR,
  input  CLK,
  output [7:0] Q
);

  wire [7:0] multiplexer_1_out;

  Multiplexer #(.Bits(8)) multiplexer_1 (.sel(CLR), .in_0(D), .in_1({8{1'b0}}), .out(multiplexer_1_out));
  Register #(.Bits(8)) register_1 (.D(multiplexer_1_out), .C(CLK), .en(LD), .Q(Q));
endmodule
