// Digital circuit SRAM.dig as structural Verilog
module SRAM (
  input  [3:0] ADDR,
  input  [7:0] DATA_IN,
  input  STORE,
  input  CLK,
  input  CLEAR,
  input  SET,
  input  LOAD,
  output [7:0] DATA
);

  wire [7:0] ramdualport_1_d, reg8_core_1_q;

  RAMDualPort #(.Bits(8)) ramdualport_1 (
    .A(ADDR[1:0]), .Din(DATA_IN), .str(STORE), .C(CLK), .ld(SET), .D(ramdualport_1_d));
  REG8_CORE reg8_core_1 (.D(ramdualport_1_d), .LD(SET), .CLR(CLEAR), .CLK(CLK), .Q(reg8_core_1_q));
  assign DATA = LOAD ? reg8_core_1_q : 8'bz;  // Driver driver_1
  // Pins of 2 and 4 bits meet at ADDR
endmodule
